# Fritzing sketch Final (saved by Fritzing 0.9.3b)
breadboards: 1

parts:
  Part4 = Arduino Ethernet Shield (Rev3)
  Part5 = KY-015 Temperature & Humidity Sensor Module [package="Breakout board"]
  R3 = PHOTOCELL [package=photocell-kit]
  R4 = Resistor [tolerance=±5% resistance=10k package="0603 [SMD]"]

nets:
  N1: Part4.A0, R3.P$2, R4.Pin_0
  N2: Part4.D2, Part5.Vin
  N3: Part4.5V, Part5.S, R3.P$1
  N4: Part4.GND, Part5.-, R4.Pin_1

custom parts:
  KY-015 Temperature & Humidity Sensor Module: KY-015 temperature and humidity sensor module, provides a low-latency serial interface to measure humidity and temperature.
