# Fritzing sketch Dht11 (saved by Fritzing 0.9.3b)
breadboards: 1

parts:
  Part2 = Arduino Ethernet Shield (Rev3)
  Part3 = KY-015 Temperature & Humidity Sensor Module [package="Breakout board"]

nets:
  N1: Part2.D2, Part3.Vin
  N2: Part2.5V, Part3.S
  N3: Part2.GND, Part3.-

custom parts:
  KY-015 Temperature & Humidity Sensor Module: KY-015 temperature and humidity sensor module, provides a low-latency serial interface to measure humidity and temperature.
